# Fritzing sketch ControllerBoard (saved by Fritzing 0.9.3b)
circuit board: 5cm x 6cm
breadboards: 1

parts:
  Part1 = Arduino Nano (Rev3.0)
  J5 = female pin header, 3 pins [form="♀ (female)"]
  S2 = Pushbutton [package="[THT]"]
  R6 = Resistor [tolerance=±5% resistance=220 package=THT]
  R7 = Resistor [tolerance=±5% resistance=220 package=THT]
  J6 = female pin header, 2 pins [form="♀ (female)"]
  J10 = female pin header, 1 pin [form="♀ (female)"]  # not connected
  J8 = female pin header, 1 pin [form="♀ (female)"]  # not connected
  J9 = female pin header, 1 pin [form="♀ (female)"]  # not connected
  J11 = female pin header, 1 pin [form="♀ (female)"]  # not connected
  Q2 = NPN-Transistor [package="TO92 [THT]"]
  J13 = female pin header, 2 pins [form="♀ (female)"]
  J4 = female pin header, 3 pins [form="♀ (female)"]
  J3 = female pin header, 3 pins [form="♀ (female)"]
  J2 = female pin header, 3 pins [form="♀ (female)"]
  S1 = Pushbutton [package="[THT]"]
  J1 = female pin header, 7 pins [form="♀ (female)"]

nets:
  N1: Part1.GND, J5.pin2, R6.Pin_1, R7.Pin_1, J13.pin1, J4.pin2, J3.pin2, J2.pin2, J1.pin2
  N2: Part1.D2, J5.pin3, J4.pin3, J3.pin3, J2.pin3
  N3: Part1.D3, Q2.B
  N4: Part1.D6, J1.pin3
  N5: Part1.D7, J1.pin4
  N6: Part1.D8, J1.pin5
  N7: Part1.D9, J1.pin6
  N8: Part1.D10, J1.pin7
  N9: Part1.D11/MOSI, S2.Pin_3, S2.Pin_4, R7.Pin_0
  N10: Part1.D12/MISO, R6.Pin_0, S1.Pin_3, S1.Pin_4
  N11: Part1.VIN, J6.pin2
  N12: Part1.5V, J5.pin1, S2.Pin_1, S2.Pin_2, J6.pin1, Q2.E, J4.pin1, J3.pin1, J2.pin1, S1.Pin_1, S1.Pin_2, J1.pin1
  N13: Q2.C, J13.pin2
