# Fritzing sketch RifleBoard (saved by Fritzing 0.9.3b)
circuit board: 5.75cm x 2.2cm
breadboards: 1

parts:
  J1 = female pin header, 3 pins [form="♀ (female)"]
  Q1 = NPN-Transistor [package="TO92 [THT]"]
  J2 = female pin header, 2 pins [form="♀ (female)"]

nets:
  N1: J1.pin1, Q1.C
  N2: J1.pin2, Q1.B
  N3: J1.pin3, J2.pin2
  N4: Q1.E, J2.pin1
